# Fritzing sketch Gun Barrel (saved by Fritzing 0.9.4)
breadboards: 1

parts:
  DFRobot_DFPlayer_Mini1 = DFRobot DFPlayer Mini [part_number=DFR0299]
  Part1 = Arduino Nano 33 IOT
  R1 = Resistor [tolerance=±5% resistance=1k package="2512 [SMD]"]
  JP1 = Header 3 [package=molex-1x3_lock]
  U1 = WS2812 RGB LED strip
  U2 = WS2812 RGB LED strip
  S1 = Momentary Switch [package=ksa_sealed_tac_switch]
  R2 = Resistor [tolerance=±5% resistance=220 package="2512 [SMD]"]

nets:
  VCC: DFRobot_DFPlayer_Mini1.VCC, Part1.VIN, U1.VCC, U2.VCC
  N1: DFRobot_DFPlayer_Mini1.RX, R1.Pin_0
  N2: DFRobot_DFPlayer_Mini1.TX, Part1.RX
  N3: DFRobot_DFPlayer_Mini1.SPK_1, JP1.3
  N4: DFRobot_DFPlayer_Mini1.GND-1, DFRobot_DFPlayer_Mini1.GND-2, R2.Pin_1
  N5: DFRobot_DFPlayer_Mini1.SPK_2, JP1.1
  N6: Part1.TX, R1.Pin_1
  N7: Part1.RESET, Part1.A7, S1.1
  GND: Part1.GND, Part1.D13~, JP1.2, U1.GND, U2.GND, U2.DIN
  N8: Part1.D11/MOSI, Part1.+5V
  N9: Part1.A0, U1.DIN
  N10: S1.2, R2.Pin_0

custom parts:
  Arduino Nano 33 IOT: The Arduino Nano 33 IoT is the easiest and cheapest point of entry to enhance existing devices (and creating new ones) to be part of the IoT and designing pico-network applications. Whether you are looking at building a sensor network connected to your office or home router, or if you want to create a BLE device sending data to a cellphone, the Nano 33 IoT is your one-stop-solution for many of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
  WS2812 RGB LED strip: WS2812 strip
